# Fritzing sketch ha_led (saved by Fritzing 0.9.2b)

parts:
  Raspberry_Pi1 = Raspberry Pi 2
  LED1 = smd LED [color="Red (633nm)" package="0603 [SMD]"]
  R1 = Resistor [tolerance=±5% resistance=220 package="0805 [SMD]"]
  Switch = SWITCH-MOMENTARY-2 [package=tactile-pth]

nets:
  N1: Raspberry_Pi1.GPIO26, R1.Pin_1
  N2: Raspberry_Pi1.GPIO21, Switch.1
  N3: LED1.cathode, R1.Pin_0
  GND: LED1.anode
  3.3V: Switch.2
